# Fritzing sketch Arduino fingerprint ID (saved by Fritzing 0.9.2b)
circuit board: 8.46667cm x 5.64444cm
breadboards: 1

parts:
  Arduino_UNO = Arduino Uno (Rev3)
  LCM1602_IIC = LCM1602 IIC [part_number="LCM1602 IIC" chip_label="LCM1602 IIC" package="DIP (Dual Inline) [THT]"]
  LCD_Display = LCD screen
  Fingerprint_Sensor = sensor_biometrico

nets:
  N1: Arduino_UNO.A4/SDA, LCM1602_IIC.SDA
  N2: Arduino_UNO.A5/SCL, LCM1602_IIC.SCL
  N3: Arduino_UNO.D2, Fingerprint_Sensor.TX
  N4: Arduino_UNO.D3_PWM, Fingerprint_Sensor.RX
  3V3: Arduino_UNO.3V3, Fingerprint_Sensor.VCC
  5V: Arduino_UNO.5V, LCM1602_IIC.VCC
  GND: Arduino_UNO.GND, LCM1602_IIC.GND, Fingerprint_Sensor.GND
  VSS: LCM1602_IIC.VSS, LCD_Display.VSS
  VDD: LCM1602_IIC.VDD, LCD_Display.VDD
  N5: LCM1602_IIC.V0, LCD_Display.V0
  N6: LCM1602_IIC.RS, LCD_Display.RS
  N7: LCM1602_IIC.RW, LCD_Display.R/W
  N8: LCM1602_IIC.E, LCD_Display.E
  N9: LCM1602_IIC.D0, LCD_Display.DB0
  N10: LCM1602_IIC.D1, LCD_Display.DB1
  N11: LCM1602_IIC.D2, LCD_Display.DB2
  N12: LCM1602_IIC.D3, LCD_Display.DB3
  N13: LCM1602_IIC.D4, LCD_Display.DB4
  N14: LCM1602_IIC.D5, LCD_Display.DB5
  N15: LCM1602_IIC.D6, LCD_Display.DB6
  N16: LCM1602_IIC.D7, LCD_Display.DB7
  N17: LCM1602_IIC.A, LCD_Display.LED+
  N18: LCM1602_IIC.K, LCD_Display.LED-
  N19: LCM1602_IIC.LED_A, LCM1602_IIC.LED_B

custom parts:
  LCM1602 IIC: I2C-Module to use a 1602 or 2004 LCD on with the wire.h libory Serial LCD Modul
  sensor_biometrico: Adafruit Optical Fingerprint Sensor

// code stored in the sketch: AnalogReadSerial2LCD_LED.ino
#include <Wire.h>
#include <LiquidCrystal_I2C.h>

LiquidCrystal_I2C lcd(0x27, 16, 2);   // adress and format LCD

const int analogInPin = A0;           // Analog input pin that the potentiometer is attached to
const int analogOutPin = 9;           // Analog output pin that the LED is attached to

int sensorValue = 0;                  // value read from the pot
int outputValue = 0;                  // value output to the PWM (analog out)

void setup() {
  lcd.init();                         // init LCD
  lcd.backlight();
  lcd.home();
  lcd.setCursor(5, 0);                // place static text
  lcd.print("ADC = ");
  lcd.setCursor(15, 0);
  lcd.print("V");
  lcd.setCursor(0, 1);
  lcd.print("LED : ");
  lcd.setCursor(12, 1);
  lcd.print("%");
  Serial.begin(9600);                 // optional serial monitor
}

void loop() {
  int sensorValue = analogRead(analogInPin);          // read analog A0 en store in sensorValue
  float voltValue = 5.0 / 1024.0 * sensorValue;       // calculate volt at analog A0 and store in voltValue
  float percentValue = sensorValue / 1024.0 * 100.0;  // calculate percentage analog A0 and store in percentValue
  outputValue = map(sensorValue, 0, 1023, 0, 255);    // map analog input to analog output and store in outputValue
  analogWrite(analogOutPin, outputValue);             // write outputValue to analogOutPin

  lcd.setCursor(0, 0);                                // set cursor at deserid position
  leadingZeros(sensorValue, 4);                       // print sensorvalue with number of leading-characters (0 or space as specified in function leadingZeros)
  lcd.setCursor(10, 0);                               // set cursor at deserid position
  lcd.print(voltValue);                               // print voltValue
  lcd.setCursor(6, 1);                                // set cursor at deserid position
  lcd.print(percentValue);                            // print percentValue

  Serial.print("sensor = " );                         // print the results to the serial monitor:
  Serial.print(sensorValue);
  Serial.print("\t output = ");
  Serial.print(outputValue);
  Serial.print("\t procent = ");
  Serial.println(percentValue);

  delay(1000);                                        // set delay
}

void leadingZeros( int value, int width) {            // display result with leading characters
  char valueStr[6];                                   // large enough to hold an int
  itoa (value, valueStr, 10);                         // itoa converts int to string
  int len = strlen(valueStr);                         // calculate length of valueStr
  if (len < width) {
    len = width - len;
    while (len--)
      lcd.print(' ');                                 // for leading zeros place '0' between (), for leading spaces place ' ' between ()
  }
  lcd.print(valueStr);
}
